# Fritzing sketch arduino-switch-3 (saved by Fritzing 0.9.3b)
circuit board: 6.03144cm x 6.02401cm

parts:
  U1 = OMRON G3MB-202p [package=relay-s108t02]
  U2 = OMRON G3MB-202p [package=relay-s108t02]
  U3 = OMRON G3MB-202p [package=relay-s108t02]
  R7 = Resistor [tolerance=±5% resistance=10k package="1206 [SMD]"]
  R6 = Resistor [tolerance=±5% resistance=10k package="1206 [SMD]"]
  R3 = Resistor [tolerance=±5% resistance=10k package="1206 [SMD]"]
  Q5 = NPN-Transistor [package="SOT-23 [SMD]"]
  Q3 = NPN-Transistor [package="SOT-23 [SMD]"]
  R2 = Resistor [tolerance=±5% resistance=10k package="1206 [SMD]"]
  R1 = Resistor [tolerance=±5% resistance=10k package="1206 [SMD]"]
  Q2 = NPN-Transistor [package="SOT-23 [SMD]"]
  R4 = Resistor [tolerance=±5% resistance=10k package="1206 [SMD]"]
  J5 = screw terminal, 4 pins
  Часть3 = Arduino Nano (Rev3.0)
  J6 = screw terminal, 4 pins

nets:
  N1: U1.T1, J6.pin2
  N2: U1.T2, U2.T2, U3.T2, J6.pin1
  N3: U1.+, U2.+, U3.+, J5.pin1, Часть3.VIN
  N4: U1.-, Q2.1
  N5: U2.T1, J6.pin3
  N6: U2.-, Q5.1
  N7: U3.T1, J6.pin4
  N8: U3.-, Q3.1
  N9: R7.Pin_0, R3.Pin_0, Q5.0
  N10: R7.Pin_1, Часть3.D7
  N11: R6.Pin_0, Q3.0, R4.Pin_0
  N12: R6.Pin_1, Часть3.D8
  N13: R3.Pin_1, Q5.2, Q3.2, R1.Pin_1, Q2.2, R4.Pin_1, J5.pin2, Часть3.GND
  N14: R2.Pin_0, R1.Pin_0, Q2.0
  N15: R2.Pin_1, Часть3.D4

notes:
  L L1 L2 L3
  + G

custom parts:
  OMRON G3MB-202p: SPST SS relay
