# Fritzing sketch arduino-switch-4 (saved by Fritzing 0.9.3b)
circuit board: 6.03144cm x 6.02401cm

parts:
  R7 = Resistor [tolerance=±5% resistance=10k package="1206 [SMD]"]
  R6 = Resistor [tolerance=±5% resistance=10k package="1206 [SMD]"]
  R3 = Resistor [tolerance=±5% resistance=10k package="1206 [SMD]"]
  Q5 = NPN-Transistor [package="SOT-23 [SMD]"]
  Q3 = NPN-Transistor [package="SOT-23 [SMD]"]
  R2 = Resistor [tolerance=±5% resistance=10k package="1206 [SMD]"]
  R1 = Resistor [tolerance=±5% resistance=10k package="1206 [SMD]"]
  Q2 = NPN-Transistor [package="SOT-23 [SMD]"]
  R4 = Resistor [tolerance=±5% resistance=10k package="1206 [SMD]"]
  J6 = screw terminal, 5 pins
  Q6 = NPN-Transistor [package="SOT-23 [SMD]"]
  R8 = Resistor [tolerance=±5% resistance=10k package="1206 [SMD]"]
  R9 = Resistor [tolerance=±5% resistance=10k package="1206 [SMD]"]
  U4 = OMRON G3MB-202p [package=relay-s108t02]
  Часть3 = Arduino Nano (Rev3.0)
  U1 = OMRON G3MB-202p [package=relay-s108t02]
  U2 = OMRON G3MB-202p [package=relay-s108t02]
  U3 = OMRON G3MB-202p [package=relay-s108t02]
  J5 = screw terminal, 4 pins

nets:
  N1: R7.Pin_0, R3.Pin_0, Q5.0
  N2: R7.Pin_1, Часть3.D7
  N3: R6.Pin_0, Q3.0, R4.Pin_0
  N4: R6.Pin_1, Часть3.D8
  N5: R3.Pin_1, Q5.2, Q3.2, R1.Pin_1, Q2.2, R4.Pin_1, Q6.2, R8.Pin_1, Часть3.GND, J5.pin2
  N6: Q5.1, U2.-
  N7: Q3.1, U3.-
  N8: R2.Pin_0, R1.Pin_0, Q2.0
  N9: R2.Pin_1, Часть3.D4
  N10: Q2.1, U1.-
  N11: J6.pin1, U4.T2, U1.T2, U2.T2, U3.T2
  N12: J6.pin2, U4.T1
  N13: J6.pin3, U1.T1
  N14: J6.pin4, U3.T1
  N15: J6.pin5, U2.T1
  N16: Q6.0, R8.Pin_0, R9.Pin_0
  N17: Q6.1, U4.-
  N18: R9.Pin_1, Часть3.D2
  N19: U4.+, Часть3.VIN, U1.+, U2.+, U3.+, J5.pin1

notes:
  + G A B
  L L1 L2 L3 L4

custom parts:
  OMRON G3MB-202p: SPST SS relay
