# Fritzing sketch arduino-switch (saved by Fritzing 0.9.3b)
circuit board: 6.99861cm x 6.99cm

parts:
  U1 = OMRON G3MB-202p [package=relay-s108t02]
  U2 = OMRON G3MB-202p [package=relay-s108t02]
  U3 = OMRON G3MB-202p [package=relay-s108t02]
  U4 = OMRON G3MB-202p [package=relay-s108t02]
  R8 = Resistor [tolerance=±5% resistance=10k package="1206 [SMD]"]
  R7 = Resistor [tolerance=±5% resistance=10k package="1206 [SMD]"]
  R6 = Resistor [tolerance=±5% resistance=10k package="1206 [SMD]"]
  R3 = Resistor [tolerance=±5% resistance=10k package="1206 [SMD]"]
  Q5 = NPN-Transistor [package="SOT-23 [SMD]"]
  Q4 = NPN-Transistor [package="SOT-23 [SMD]"]
  Q3 = NPN-Transistor [package="SOT-23 [SMD]"]
  R2 = Resistor [tolerance=±5% resistance=10k package="1206 [SMD]"]
  R1 = Resistor [tolerance=±5% resistance=10k package="1206 [SMD]"]
  Q2 = NPN-Transistor [package="SOT-23 [SMD]"]
  R4 = Resistor [tolerance=±5% resistance=10k package="1206 [SMD]"]
  R5 = Resistor [tolerance=±5% resistance=10k package="1206 [SMD]"]
  Часть2 = Arduino Nano (Rev3.0) (ICSP)
  J4 = screw terminal, 5 pins
  J5 = screw terminal, 4 pins

nets:
  N1: U1.T1, J4.pin3
  N2: U1.T2, U2.T2, U3.T2, U4.T2, J4.pin1
  N3: U1.+, U2.+, U3.+, U4.+, Часть2.VIN, J5.pin1
  N4: U1.-, Q2.1
  N5: U2.T1, J4.pin2
  N6: U2.-, Q5.1
  N7: U3.T1, J4.pin4
  N8: U3.-, Q3.1
  N9: U4.T1, J4.pin5
  N10: U4.-, Q4.1
  N11: R8.Pin_0, Q4.0, R5.Pin_0
  N12: R8.Pin_1, Часть2.D5
  N13: R7.Pin_0, R3.Pin_0, Q5.0
  N14: R7.Pin_1, Часть2.D3
  N15: R6.Pin_0, Q3.0, R4.Pin_0
  N16: R6.Pin_1, Часть2.D4
  N17: R3.Pin_1, Q5.2, Q4.2, Q3.2, R1.Pin_1, Q2.2, R4.Pin_1, R5.Pin_1, Часть2.GND, J5.pin2
  N18: R2.Pin_0, R1.Pin_0, Q2.0
  N19: R2.Pin_1, Часть2.D2

notes:
  L L1 L2 L3 L4
  + G

custom parts:
  OMRON G3MB-202p: SPST SS relay
